# Fritzing sketch Control_Digital (saved by Fritzing 1.0.8)

parts:
  J1 = DHT22 temperature-humidity sensor [form="♂ (male)" package=THT]
  M3 = BTS7960  # not connected
  BAT2 = 12 battery [package=battery]
  M4 = ESP32-S3-DevKitC-1-N8R8-v1 [part_number=ESP32-S3-DevKitC-1-N8R8-v1]
  A2 = WMYCONGCONG buck converter
  M5 = BTS7960  # not connected

nets:
  N1: J1.VCC, M4.pin_1, M4.pin_2, A2.Pin_1
  N2: J1.GND, M4.pin_22, M4.pin_44, A2.Pin_4
  N3: BAT2.-, A2.Pin_3
  N4: BAT2.+, A2.Pin_2

custom parts:
  DHT22 temperature-humidity sensor: The DHT22 is a basic, low-cost digital temperature and humidity sensor. It uses a capacitive humidity sensor and a thermistor to measure the surrounding air, and spits out a digital signal on the data pin (no analog input pins needed). It's fairly simple to use, but requires careful timing to grab data. The only real downside of this sensor is you can only get new data from it once every 2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
  BTS7960: BTS7960 43A Peak Power H-Bridge PWM Motor Driver
  12 battery: 12V lead acid type battery, like the Husqvarna YTH2448 12V 35AH battery. This is the mini version 1/4 the size of the actual battery to be closer to typical breadboard parts (around 2in wide rathher than 7in). The pads in pcb are sized to accomidate up to 14ga wire (as these batterys will deliver high currents.)
  ESP32-S3-DevKitC-1-N8R8-v1: ESP32-S3-DevKitC-1-N8R8-v1 This module is 44pins long (2x22) and 11 pins width.
  WMYCONGCONG buck converter: These amazing little DC-DC converters feature a wide input voltage of 4.5-24V and the output voltage can be set to one of six fixed voltages, or fully variable, just by bridging the relevant solder pads on the back of the PCB..
